# Fritzing sketch speaker_power (saved by Fritzing 0.9.3b)

parts:
  Raspberry_Pi1 = Raspberry Pi B+
  4_Channel_Relay2 = 4 Channel Power Relay
  Power_plug1 = Power plug
  SPKR1 = Loudspeaker

nets:
  N1: Raspberry_Pi1.GPIO15, 4_Channel_Relay2.IN2
  N2: Raspberry_Pi1.GPIO14, 4_Channel_Relay2.IN1
  GND: Raspberry_Pi1.GND, 4_Channel_Relay2.GND
  N3: Raspberry_Pi1.5V, 4_Channel_Relay2.VCC#13
  N4: 4_Channel_Relay2.VCC#14, 4_Channel_Relay2.JD-VCC
  N5: 4_Channel_Relay2.COM, Power_plug1.VCC
  N6: 4_Channel_Relay2.NO, SPKR1.pin2
  N7: Power_plug1.GND, SPKR1.pin1

custom parts:
  4 Channel Power Relay: A 4 channel power relay. The module operates at 5V.
